# Fritzing sketch lunar vehicle (saved by Fritzing 0.8.7b)
breadboards: 1

parts:
  Part1 = Arduino Mega 2560 (Rev3)
  RHT1 = Humidity and Temperature Sensor RHT03
  LED1 = RGB LED (com. anode, rbg) [package="5 mm [THT]"]
  LED2 = RGB LED (com. anode, rbg) [package="5 mm [THT]"]
  LED3 = RGB LED (com. anode, rbg) [package="5 mm [THT]"]
  LED4 = RGB LED (com. anode, rbg) [package="5 mm [THT]"]
  LED5 = RGB LED (com. anode, rbg) [package="5 mm [THT]"]
  LED6 = RGB LED (com. anode, rbg) [package="5 mm [THT]"]
  U3 = TCM8240MD [package=tcm8240md]  # not connected
  MD03A1 = Dual VNH2SP30 Motor Driver [part_number=MD03A]
  M2 = DC Motor
  M3 = DC Motor
  MD03A2 = Dual VNH2SP30 Motor Driver [part_number=MD03A]
  M4 = DC Motor
  M5 = DC Motor
  MD03A3 = Dual VNH2SP30 Motor Driver [part_number=MD03A]
  M6 = DC Motor
  M7 = DC Motor
  Part2 = Thumb Joystick
  J1 = Piezo Speaker
  J2 = Basic Servo
  U4 = SPM0204UD5 [package=spm0204ud5]
  U5 = HDJD-S822-QR999 [package=qfn-16-(rounded0thermal-pad)]
  LED7 = RGB LED (com. anode, rbg) [package="5 mm [THT]"]

nets:
  N1: Part1.A8, U5.VROUT
  N2: Part1.A9, U5.VGOUT
  N3: Part1.A10, U5.VBOUT
  N4: Part1.A0, Part2.VERT
  N5: Part1.A1, Part2.HORZ
  N6: Part1.A3, RHT1.Data-signal
  N7: Part1.A5, U4.OUT
  N8: Part1.D13_PWM, LED1.red_cathode, LED2.red_cathode, LED6.red_cathode
  N9: Part1.D12_PWM, LED1.green_cathode, LED2.green_cathode, LED6.green_cathode
  N10: Part1.D11_PWM, LED1.blue_cathode, LED2.blue_cathode, LED6.blue_cathode
  N11: Part1.D10_PWM, LED4.red_cathode, LED5.red_cathode
  N12: Part1.D9_PWM, LED4.green_cathode, LED5.green_cathode
  N13: Part1.D8_PWM, LED4.blue_cathode, LED5.blue_cathode
  N14: Part1.3V3, LED1.common_anode, LED2.common_anode, LED4.common_anode, LED5.common_anode, LED6.common_anode, LED7.common_anode
  VCC: Part1.5V, RHT1.Vcc, LED3.common_anode, MD03A1.+5V_(IN), MD03A1.VIN, MD03A2.VIN, MD03A3.VIN, Part2.VCC, J2.vcc
  GND: Part1.GND, RHT1.GND_1, RHT1.GND_2, MD03A1.GND, MD03A2.GND, MD03A3.GND, Part2.GND, J1.pin1, J2.gnd, U4.GND, U4.GND#, U5.GND
  N15: Part1.D0_RX0, LED7.blue_cathode
  N16: Part1.D1_TX0, LED7.green_cathode
  N17: Part1.D2_PWM, LED7.red_cathode
  N18: Part1.D3_PWM, LED3.blue_cathode
  N19: Part1.D4_PWM, LED3.green_cathode
  N20: Part1.D5_PWM, LED3.red_cathode
  N21: Part1.D7_PWM, J2.pulse
  N22: Part1.D22, MD03A1.1INa
  N23: Part1.D23, MD03A1.2INb
  N24: Part1.D24, MD03A2.1INa
  N25: Part1.D25, MD03A2.2INb
  N26: Part1.D26, MD03A3.1INa
  N27: Part1.D27, MD03A3.2INb
  N28: Part1.D28, U4.VS
  N29: Part1.D52, J1.pin2
  N30: Part1.D53, Part2.SEL
  N31: MD03A1.OUT_1A, M3.pin_1
  N32: MD03A1.OUT_1B, M3.pin_2
  N33: MD03A1.OUT_2A, M2.pin_1
  N34: MD03A1.OUT_2B, M2.pin_2
  N35: MD03A2.OUT_1A, M4.pin_1
  N36: MD03A2.OUT_1B, M4.pin_2
  N37: MD03A2.OUT_2A, M5.pin_1
  N38: MD03A2.OUT_2B, M5.pin_2
  N39: MD03A3.OUT_1A, M6.pin_1
  N40: MD03A3.OUT_1B, M6.pin_2
  N41: MD03A3.OUT_2A, M7.pin_1
  N42: MD03A3.OUT_2B, M7.pin_2
